// Logisim project nand2tetris.circ as structural Verilog
module gate_NOT (
  input  in_1,
  output out_2
);

  nand nand_1 (out_2, in_1, in_1);
endmodule

module gate_AND (
  input  in_1,
  input  in_2,
  output out_3
);

  wire nand_1_out;

  nand nand_1 (nand_1_out, in_1, in_2);
  not not_1 (out_3, nand_1_out);
endmodule

module gate_OR (
  input  in_1,
  input  in_2,
  output out_3
);

  wire not_1_out, not_2_out;

  not not_1 (not_1_out, in_1);
  not not_2 (not_2_out, in_2);
  nand nand_1 (out_3, not_1_out, not_2_out);
endmodule

module gate_XOR (
  input  in_1,
  input  in_2,
  output out_3
);

  wire and_1_out, not_1_out, or_1_out;

  and and_1 (and_1_out, in_1, in_2);
  or or_1 (or_1_out, in_1, in_2);
  not not_1 (not_1_out, and_1_out);
  and and_2 (out_3, not_1_out, or_1_out);
endmodule

module plexer_MUX (
  input  In0,
  input  Sel,
  input  In1,
  output out0
);

  wire nand_1_out, nand_2_out, not_1_out;

  not not_1 (not_1_out, Sel);
  nand nand_1 (nand_1_out, In0, not_1_out);
  nand nand_2 (nand_2_out, In1, Sel);
  nand nand_3 (out0, nand_1_out, nand_2_out);
endmodule

module plexer_DMUX (
  input  in0,
  input  sel,
  output out0,
  output out1
);
endmodule
