// Logisim project nand2tetris.circ as structural Verilog
module gate_NOT (
  input  in0,
  output out0
);

  nand nand_1 (out0, in0, in0);
endmodule

module gate_AND (
  input  in_1,
  input  in_2,
  output out_3
);

  wire nand_1_out;

  nand nand_1 (nand_1_out, in_1, in_2);
  not not_1 (out_3, nand_1_out);
endmodule

module gate_OR (
  input  in_1,
  input  in_2,
  output out_3
);

  // AND_Gate and_1 is placed but not wired
  // AND_Gate and_2 is placed but not wired
  // AND_Gate and_3 is placed but not wired
endmodule
